# Fritzing sketch openbot-diy-esp32-breadboard (saved by Fritzing 1.0.8)

parts:
  ESP32_DevKit = ESP32 DevKit
  L298N = L298N
  M1_·_левый_передний = M1 · левый передний
  M2_·_левый_задний = M2 · левый задний
  M3_·_правый_передний = M3 · правый передний
  M4_·_правый_задний = M4 · правый задний
  3_×_18650_·_3S = 3 × 18650 · 3S
  SW1_·_питание = SW1 · питание
  DC/DC_·_логика = DC/DC · логика
  DC/DC_·_моторы_* = DC/DC · моторы *
  LM393_·_левый = LM393 · левый
  LM393_·_правый = LM393 · правый
  HC-SR04+ = HC-SR04+
  R1 = R1 [resistance="30 кОм"]
  R2 = R2 [resistance="10 кОм"]
  R3 = R3 [resistance="1 кОм"]
  R4 = R4 [resistance="2 кОм"]
  R5 = R5 [resistance="10 кОм"]
  R6 = R6 [resistance="10 кОм"]
  OpenBot_DIY_·_ESP32 = OpenBot DIY · ESP32  # not connected
  Конфигурация_прошивки = Конфигурация прошивки  # not connected
  Питание = Питание  # not connected
  Примечания = Примечания  # not connected
  Цвета_проводов = Цвета проводов  # not connected
  Соединение_VBAT = Соединение VBAT
  Соединение_ADC = Соединение ADC
  Соединение_5V = Соединение 5V
  Соединение_5V_2 = Соединение 5V
  Соединение_3V3 = Соединение 3V3
  Соединение_3V3_2 = Соединение 3V3
  Соединение_3V3_3 = Соединение 3V3
  Соединение_GND = Соединение GND
  Соединение_GND_2 = Соединение GND
  Соединение_GND_3 = Соединение GND
  Соединение_GND_4 = Соединение GND
  Соединение_GND_5 = Соединение GND
  Соединение_GND_6 = Соединение GND
  Соединение_GND_7 = Соединение GND
  Соединение_GND_8 = Соединение GND
  Соединение_encoder = Соединение encoder
  Соединение_encoder_2 = Соединение encoder
  Соединение_sonar = Соединение sonar

nets:
  N1: ESP32_DevKit.GPIO4, R1.2, R2.1, Соединение_ADC.junction
  N2: ESP32_DevKit.GPIO13, L298N.IN1
  N3: ESP32_DevKit.GPIO12, L298N.IN2
  N4: ESP32_DevKit.GPIO15, L298N.IN3
  N5: ESP32_DevKit.GPIO2, L298N.IN4
  GND: ESP32_DevKit.GND2, ESP32_DevKit.GND3, ESP32_DevKit.GND, L298N.GND, 3_×_18650_·_3S.GND, DC/DC_·_логика.GND, DC/DC_·_моторы_*.GND, LM393_·_левый.GND, LM393_·_правый.GND, HC-SR04+.GND, R2.2, R4.2, Соединение_GND.junction, Соединение_GND_2.junction, Соединение_GND_3.junction, Соединение_GND_4.junction, Соединение_GND_5.junction, Соединение_GND_6.junction, Соединение_GND_7.junction, Соединение_GND_8.junction
  N6: ESP32_DevKit.GPIO35, LM393_·_левый.D0, R5.2, Соединение_encoder.junction
  N7: ESP32_DevKit.GPIO22, LM393_·_правый.D0, R6.2, Соединение_encoder_2.junction
  N8: ESP32_DevKit.GPIO5, HC-SR04+.Trig
  N9: ESP32_DevKit.GPIO18, R3.1, R4.1, Соединение_sonar.junction
  5V: ESP32_DevKit.5V, L298N.5V, L298N.ENA, L298N.ENB, DC/DC_·_логика.OUT+, HC-SR04+.VCC, Соединение_5V.junction, Соединение_5V_2.junction
  VCC: ESP32_DevKit.3V3, LM393_·_левый.VCC, LM393_·_правый.VCC, R5.1, R6.1, Соединение_3V3.junction, Соединение_3V3_2.junction, Соединение_3V3_3.junction
  N10: L298N.OUT1, M1_·_левый_передний.+, M2_·_левый_задний.+
  N11: L298N.OUT2, M1_·_левый_передний.−, M2_·_левый_задний.−
  N12: L298N.OUT3, M3_·_правый_передний.−, M4_·_правый_задний.−
  N13: L298N.OUT4, M3_·_правый_передний.+, M4_·_правый_задний.+
  N14: L298N.+12V, DC/DC_·_моторы_*.OUT+
  N15: 3_×_18650_·_3S.+, SW1_·_питание.IN, SW1_·_питание.OUT, DC/DC_·_логика.IN+, DC/DC_·_моторы_*.IN+, R1.1, Соединение_VBAT.junction
  N16: HC-SR04+.Echo, R3.2

custom parts:
  ESP32 DevKit: OpenBot DIY physical Breadboard illustration; pin order is board-specific. See README.breadboard.ru-RU.md. License: CC BY-SA 3.0.
  L298N: OpenBot DIY physical Breadboard illustration; pin order is board-specific. See README.breadboard.ru-RU.md. License: CC BY-SA 3.0.
  M1 · левый передний: OpenBot DIY physical Breadboard illustration; pin order is board-specific. See README.breadboard.ru-RU.md. License: CC BY-SA 3.0.
  M2 · левый задний: OpenBot DIY physical Breadboard illustration; pin order is board-specific. See README.breadboard.ru-RU.md. License: CC BY-SA 3.0.
  M3 · правый передний: OpenBot DIY physical Breadboard illustration; pin order is board-specific. See README.breadboard.ru-RU.md. License: CC BY-SA 3.0.
  M4 · правый задний: OpenBot DIY physical Breadboard illustration; pin order is board-specific. See README.breadboard.ru-RU.md. License: CC BY-SA 3.0.
  3 × 18650 · 3S: OpenBot DIY physical Breadboard illustration; pin order is board-specific. See README.breadboard.ru-RU.md. License: CC BY-SA 3.0.
  SW1 · питание: OpenBot DIY physical Breadboard illustration; pin order is board-specific. See README.breadboard.ru-RU.md. License: CC BY-SA 3.0.
  DC/DC · логика: OpenBot DIY physical Breadboard illustration; pin order is board-specific. See README.breadboard.ru-RU.md. License: CC BY-SA 3.0.
  DC/DC · моторы *: OpenBot DIY physical Breadboard illustration; pin order is board-specific. See README.breadboard.ru-RU.md. License: CC BY-SA 3.0.
  LM393 · левый: OpenBot DIY physical Breadboard illustration; pin order is board-specific. See README.breadboard.ru-RU.md. License: CC BY-SA 3.0.
  LM393 · правый: OpenBot DIY physical Breadboard illustration; pin order is board-specific. See README.breadboard.ru-RU.md. License: CC BY-SA 3.0.
  HC-SR04+: OpenBot DIY physical Breadboard illustration; pin order is board-specific. See README.breadboard.ru-RU.md. License: CC BY-SA 3.0.
  R1: OpenBot DIY physical Breadboard illustration; pin order is board-specific. See README.breadboard.ru-RU.md. License: CC BY-SA 3.0.
  R2: OpenBot DIY physical Breadboard illustration; pin order is board-specific. See README.breadboard.ru-RU.md. License: CC BY-SA 3.0.
  R3: OpenBot DIY physical Breadboard illustration; pin order is board-specific. See README.breadboard.ru-RU.md. License: CC BY-SA 3.0.
  R4: OpenBot DIY physical Breadboard illustration; pin order is board-specific. See README.breadboard.ru-RU.md. License: CC BY-SA 3.0.
  R5: OpenBot DIY physical Breadboard illustration; pin order is board-specific. See README.breadboard.ru-RU.md. License: CC BY-SA 3.0.
  R6: OpenBot DIY physical Breadboard illustration; pin order is board-specific. See README.breadboard.ru-RU.md. License: CC BY-SA 3.0.
  OpenBot DIY · ESP32: OpenBot DIY physical Breadboard illustration; pin order is board-specific. See README.breadboard.ru-RU.md. License: CC BY-SA 3.0.
  Конфигурация прошивки: OpenBot DIY physical Breadboard illustration; pin order is board-specific. See README.breadboard.ru-RU.md. License: CC BY-SA 3.0.
  Питание: OpenBot DIY physical Breadboard illustration; pin order is board-specific. See README.breadboard.ru-RU.md. License: CC BY-SA 3.0.
  Примечания: OpenBot DIY physical Breadboard illustration; pin order is board-specific. See README.breadboard.ru-RU.md. License: CC BY-SA 3.0.
  Цвета проводов: OpenBot DIY physical Breadboard illustration; pin order is board-specific. See README.breadboard.ru-RU.md. License: CC BY-SA 3.0.
  Соединение VBAT: Native electrical branch contact; CC BY-SA 3.0.
  Соединение ADC: Native electrical branch contact; CC BY-SA 3.0.
  Соединение 5V: Native electrical branch contact; CC BY-SA 3.0.
  Соединение 3V3: Native electrical branch contact; CC BY-SA 3.0.
  Соединение GND: Native electrical branch contact; CC BY-SA 3.0.
  Соединение encoder: Native electrical branch contact; CC BY-SA 3.0.
  Соединение sonar: Native electrical branch contact; CC BY-SA 3.0.
