# Fritzing sketch openbot-diy-esp32 (saved by Fritzing 1.0.8)

parts:
  ESP32_DevKit = ESP32 DevKit
  L298N = L298N
  M1_·_левый_передний = M1 · левый передний
  M2_·_левый_задний = M2 · левый задний
  M3_·_правый_передний = M3 · правый передний
  M4_·_правый_задний = M4 · правый задний
  3_×_18650_·_3S = 3 × 18650 · 3S
  SW1_·_питание = SW1 · питание
  DC/DC_·_логика = DC/DC · логика
  DC/DC_·_моторы_* = DC/DC · моторы *
  LM393_·_левый = LM393 · левый
  LM393_·_правый = LM393 · правый
  HC-SR04+ = HC-SR04+
  R1 = R1 [resistance="30 кОм"]
  R2 = R2 [resistance="10 кОм"]
  R3 = R3 [resistance="1 кОм"]
  R4 = R4 [resistance="2 кОм"]
  R5 = R5 [resistance="10 кОм"]
  R6 = R6 [resistance="10 кОм"]
  OpenBot_DIY_·_ESP32 = OpenBot DIY · ESP32  # not connected
  Конфигурация_прошивки = Конфигурация прошивки  # not connected
  Питание = Питание  # not connected
  Примечания = Примечания  # not connected
  Цвета_проводов = Цвета проводов  # not connected
  Распределитель_6_×_2 = Распределитель 6 × 2

nets:
  N1: ESP32_DevKit.GPIO4, R1.2, R2.1
  N2: ESP32_DevKit.GPIO13, L298N.IN1
  N3: ESP32_DevKit.GPIO12, L298N.IN2
  N4: ESP32_DevKit.GPIO15, L298N.IN3
  N5: ESP32_DevKit.GPIO2, L298N.IN4
  GND: ESP32_DevKit.GND2, ESP32_DevKit.GND3, ESP32_DevKit.GND, L298N.GND, 3_×_18650_·_3S.GND, DC/DC_·_логика.GND, DC/DC_·_моторы_*.GND, LM393_·_левый.GND, LM393_·_правый.GND, HC-SR04+.GND, R2.2, R4.2, Распределитель_6_×_2.GND1
  N6: ESP32_DevKit.GPIO35, LM393_·_левый.D0, R5.2
  N7: ESP32_DevKit.GPIO22, LM393_·_правый.D0, R6.2
  N8: ESP32_DevKit.GPIO5, HC-SR04+.Trig
  N9: ESP32_DevKit.GPIO18, R3.1, R4.1
  5V: ESP32_DevKit.5V, L298N.5V, L298N.ENA, L298N.ENB, DC/DC_·_логика.OUT+, HC-SR04+.VCC, Распределитель_6_×_2.5V1
  VCC: ESP32_DevKit.3V3, LM393_·_левый.VCC, LM393_·_правый.VCC, R5.1, R6.1
  N10: L298N.OUT1, M1_·_левый_передний.+, M2_·_левый_задний.+
  N11: L298N.OUT2, M1_·_левый_передний.−, M2_·_левый_задний.−
  N12: L298N.OUT3, M3_·_правый_передний.−, M4_·_правый_задний.−
  N13: L298N.OUT4, M3_·_правый_передний.+, M4_·_правый_задний.+
  N14: L298N.+12V, DC/DC_·_моторы_*.OUT+
  N15: 3_×_18650_·_3S.+, SW1_·_питание.IN, SW1_·_питание.OUT, DC/DC_·_логика.IN+, DC/DC_·_моторы_*.IN+, R1.1
  N16: HC-SR04+.Echo, R3.2

custom parts:
  ESP32 DevKit: OpenBot DIY functional wiring symbol. Pin names identify contacts; positions are schematic. License: CC BY-SA 3.0.
  L298N: OpenBot DIY functional wiring symbol. Pin names identify contacts; positions are schematic. License: CC BY-SA 3.0.
  M1 · левый передний: OpenBot DIY functional wiring symbol. Pin names identify contacts; positions are schematic. License: CC BY-SA 3.0.
  M2 · левый задний: OpenBot DIY functional wiring symbol. Pin names identify contacts; positions are schematic. License: CC BY-SA 3.0.
  M3 · правый передний: OpenBot DIY functional wiring symbol. Pin names identify contacts; positions are schematic. License: CC BY-SA 3.0.
  M4 · правый задний: OpenBot DIY functional wiring symbol. Pin names identify contacts; positions are schematic. License: CC BY-SA 3.0.
  3 × 18650 · 3S: OpenBot DIY functional wiring symbol. Pin names identify contacts; positions are schematic. License: CC BY-SA 3.0.
  SW1 · питание: OpenBot DIY functional wiring symbol. Pin names identify contacts; positions are schematic. License: CC BY-SA 3.0.
  DC/DC · логика: OpenBot DIY functional wiring symbol. Pin names identify contacts; positions are schematic. License: CC BY-SA 3.0.
  DC/DC · моторы *: OpenBot DIY functional wiring symbol. Pin names identify contacts; positions are schematic. License: CC BY-SA 3.0.
  LM393 · левый: OpenBot DIY functional wiring symbol. Pin names identify contacts; positions are schematic. License: CC BY-SA 3.0.
  LM393 · правый: OpenBot DIY functional wiring symbol. Pin names identify contacts; positions are schematic. License: CC BY-SA 3.0.
  HC-SR04+: OpenBot DIY functional wiring symbol. Pin names identify contacts; positions are schematic. License: CC BY-SA 3.0.
  R1: OpenBot DIY functional wiring symbol. Pin names identify contacts; positions are schematic. License: CC BY-SA 3.0.
  R2: OpenBot DIY functional wiring symbol. Pin names identify contacts; positions are schematic. License: CC BY-SA 3.0.
  R3: OpenBot DIY functional wiring symbol. Pin names identify contacts; positions are schematic. License: CC BY-SA 3.0.
  R4: OpenBot DIY functional wiring symbol. Pin names identify contacts; positions are schematic. License: CC BY-SA 3.0.
  R5: OpenBot DIY functional wiring symbol. Pin names identify contacts; positions are schematic. License: CC BY-SA 3.0.
  R6: OpenBot DIY functional wiring symbol. Pin names identify contacts; positions are schematic. License: CC BY-SA 3.0.
  OpenBot DIY · ESP32: OpenBot DIY functional wiring symbol. Pin names identify contacts; positions are schematic. License: CC BY-SA 3.0.
  Конфигурация прошивки: OpenBot DIY functional wiring symbol. Pin names identify contacts; positions are schematic. License: CC BY-SA 3.0.
  Питание: OpenBot DIY functional wiring symbol. Pin names identify contacts; positions are schematic. License: CC BY-SA 3.0.
  Примечания: OpenBot DIY functional wiring symbol. Pin names identify contacts; positions are schematic. License: CC BY-SA 3.0.
  Цвета проводов: OpenBot DIY functional wiring symbol. Pin names identify contacts; positions are schematic. License: CC BY-SA 3.0.
  Распределитель 6 × 2: 6 x 2 header on perfboard: solder each row separately; one bus 5V, one bus GND. Never join the rows.
