# Fritzing sketch openbot-diy-nano-breadboard (saved by Fritzing 1.0.8)

parts:
  Arduino_Nano = Arduino Nano [part_number="Arduino Nano"]
  L298N = L298N [part_number=L298N]
  M1_·_левый_передний = M1 · левый передний [part_number="M1 · левый передний"]
  M2_·_левый_задний = M2 · левый задний [part_number="M2 · левый задний"]
  M3_·_правый_передний = M3 · правый передний [part_number="M3 · правый передний"]
  M4_·_правый_задний = M4 · правый задний [part_number="M4 · правый задний"]
  3_×_18650_·_3S = 3 × 18650 · 3S [part_number="3 × 18650 · 3S"]
  SW1_·_питание = SW1 · питание [part_number="SW1 · питание"]
  LM393_·_левый = LM393 · левый [part_number="LM393 · левый"]
  LM393_·_правый = LM393 · правый [part_number="LM393 · правый"]
  HC-SR04 = HC-SR04 [part_number=HC-SR04]
  OLED_·_SSD1306 = OLED · SSD1306 [part_number="OLED · SSD1306"]
  R1 = R1 [resistance="20 кОм" part_number=R1]
  R2 = R2 [resistance="10 кОм" part_number=R2]
  R3 = R3 [resistance="150 Ом" part_number=R3]
  LED_L_·_левый = LED L · левый [part_number="LED L · левый"]
  R4 = R4 [resistance="150 Ом" part_number=R4]
  LED_R_·_правый = LED R · правый [part_number="LED R · правый"]
  OpenBot_DIY_·_Arduino_Nano = OpenBot DIY · Arduino Nano [part_number="OpenBot DIY · Arduino Nano"]  # not connected
  Примечания = Примечания [part_number=Примечания]  # not connected
  Цвета_проводов = Цвета проводов  # not connected
  Распределитель_6_×_2 = Распределитель 6 × 2
  Соединение_VBAT = Соединение VBAT
  Соединение_ADC = Соединение ADC

nets:
  GND: Arduino_Nano.GND, Arduino_Nano.GND2, L298N.GND, 3_×_18650_·_3S.GND, LM393_·_левый.GND, LM393_·_правый.GND, HC-SR04.GND, OLED_·_SSD1306.GND, R2.2, LED_L_·_левый.K, LED_R_·_правый.K, Распределитель_6_×_2.GND1, Распределитель_6_×_2.GND2, Распределитель_6_×_2.GND3, Распределитель_6_×_2.GND4, Распределитель_6_×_2.GND5, Распределитель_6_×_2.GND6
  N1: Arduino_Nano.RST1, Arduino_Nano.RST2
  N2: Arduino_Nano.A7, R1.2, R2.1, Соединение_ADC.junction
  N3: Arduino_Nano.D5, L298N.IN1
  N4: Arduino_Nano.D6, L298N.IN2
  N5: Arduino_Nano.D9, L298N.IN3
  N6: Arduino_Nano.D10, L298N.IN4
  N7: Arduino_Nano.D4, R3.1
  N8: Arduino_Nano.D7, R4.1
  N9: Arduino_Nano.D2, LM393_·_левый.D0
  N10: Arduino_Nano.D3, LM393_·_правый.D0
  N11: Arduino_Nano.D12, HC-SR04.Trig
  N12: Arduino_Nano.D11, HC-SR04.Echo
  N13: Arduino_Nano.A5, OLED_·_SSD1306.SCL
  N14: Arduino_Nano.A4, OLED_·_SSD1306.SDA
  N15: L298N.OUT1, M1_·_левый_передний.+, M2_·_левый_задний.+
  N16: L298N.OUT2, M1_·_левый_передний.−, M2_·_левый_задний.−
  N17: L298N.OUT3, M3_·_правый_передний.−, M4_·_правый_задний.−
  N18: L298N.OUT4, M3_·_правый_передний.+, M4_·_правый_задний.+
  N19: L298N.+12V, 3_×_18650_·_3S.+, SW1_·_питание.IN, SW1_·_питание.OUT, R1.1, Соединение_VBAT.junction
  VCC: L298N.5V, L298N.ENA, L298N.ENB, LM393_·_левый.VCC, LM393_·_правый.VCC, HC-SR04.VCC, OLED_·_SSD1306.VCC, Распределитель_6_×_2.5V1, Распределитель_6_×_2.5V2, Распределитель_6_×_2.5V3, Распределитель_6_×_2.5V4, Распределитель_6_×_2.5V5, Распределитель_6_×_2.5V6
  N20: R3.2, LED_L_·_левый.A
  N21: R4.2, LED_R_·_правый.A

custom parts:
  Arduino Nano: OpenBot DIY: bundled Fritzing library artwork adapted to the existing connector IDs. Original author and license: library-parts/sources.json. See README.breadboard.ru-RU.md. Source: https://github.com/fritzing/fritzing-parts/blob/develop/core/Arduino Nano3(fix).fzp; CC BY-SA 3.0
  L298N: OpenBot DIY: bundled Fritzing library artwork adapted to the existing connector IDs. Original author and license: library-parts/sources.json. See README.breadboard.ru-RU.md. Source: https://github.com/coderfls/Fritzing-Parts; Published Fritzing part; no explicit license in FZP
  M1 · левый передний: OpenBot DIY: bundled Fritzing library artwork adapted to the existing connector IDs. Original author and license: library-parts/sources.json. See README.breadboard.ru-RU.md. Source: https://github.com/fritzing/fritzing-parts/blob/develop/core/gear-motor_2.fzp; CC BY-SA 3.0
  M2 · левый задний: OpenBot DIY: bundled Fritzing library artwork adapted to the existing connector IDs. Original author and license: library-parts/sources.json. See README.breadboard.ru-RU.md. Source: https://github.com/fritzing/fritzing-parts/blob/develop/core/gear-motor_2.fzp; CC BY-SA 3.0
  M3 · правый передний: OpenBot DIY: bundled Fritzing library artwork adapted to the existing connector IDs. Original author and license: library-parts/sources.json. See README.breadboard.ru-RU.md. Source: https://github.com/fritzing/fritzing-parts/blob/develop/core/gear-motor_2.fzp; CC BY-SA 3.0
  M4 · правый задний: OpenBot DIY: bundled Fritzing library artwork adapted to the existing connector IDs. Original author and license: library-parts/sources.json. See README.breadboard.ru-RU.md. Source: https://github.com/fritzing/fritzing-parts/blob/develop/core/gear-motor_2.fzp; CC BY-SA 3.0
  3 × 18650 · 3S: OpenBot DIY: bundled Fritzing library artwork adapted to the existing connector IDs. Original author and license: library-parts/sources.json. See README.breadboard.ru-RU.md. Source: https://forum.fritzing.org/t/18650-battery-holder-part-design/6523/32; Published Fritzing part; no explicit license in FZP
  SW1 · питание: OpenBot DIY: bundled Fritzing library artwork adapted to the existing connector IDs. Original author and license: library-parts/sources.json. See README.breadboard.ru-RU.md. Source: https://github.com/fritzing/fritzing-parts/blob/develop/core/basic-toggle-switch.fzp; CC BY-SA 3.0
  LM393 · левый: OpenBot DIY: bundled Fritzing library artwork adapted to the existing connector IDs. Original author and license: library-parts/sources.json. See README.breadboard.ru-RU.md. Source: https://forum.fritzing.org/t/fc-03-ir-speed-sensor/5137/3; Published Fritzing part; no explicit license in FZP
  LM393 · правый: OpenBot DIY: bundled Fritzing library artwork adapted to the existing connector IDs. Original author and license: library-parts/sources.json. See README.breadboard.ru-RU.md. Source: https://forum.fritzing.org/t/fc-03-ir-speed-sensor/5137/3; Published Fritzing part; no explicit license in FZP
  HC-SR04: OpenBot DIY: bundled Fritzing library artwork adapted to the existing connector IDs. Original author and license: library-parts/sources.json. See README.breadboard.ru-RU.md. Source: https://github.com/fritzing/fritzing-parts/blob/develop/core/hc-sr04_bf8299a_002.fzp; CC BY-SA 3.0
  OLED · SSD1306: OpenBot DIY: bundled Fritzing library artwork adapted to the existing connector IDs. Original author and license: library-parts/sources.json. See README.breadboard.ru-RU.md. Source: https://github.com/TD-er/fritzing-parts/tree/master/OLED_SSD1306_I2C_128x64; MIT
  R1: OpenBot DIY: bundled Fritzing library artwork adapted to the existing connector IDs. Original author and license: library-parts/sources.json. See README.breadboard.ru-RU.md. Source: https://github.com/fritzing/fritzing-parts/blob/develop/core/resistor.fzp; CC BY-SA 3.0
  R2: OpenBot DIY: bundled Fritzing library artwork adapted to the existing connector IDs. Original author and license: library-parts/sources.json. See README.breadboard.ru-RU.md. Source: https://github.com/fritzing/fritzing-parts/blob/develop/core/resistor.fzp; CC BY-SA 3.0
  R3: OpenBot DIY: bundled Fritzing library artwork adapted to the existing connector IDs. Original author and license: library-parts/sources.json. See README.breadboard.ru-RU.md. Source: https://github.com/fritzing/fritzing-parts/blob/develop/core/resistor.fzp; CC BY-SA 3.0
  LED L · левый: OpenBot DIY: bundled Fritzing library artwork adapted to the existing connector IDs. Original author and license: library-parts/sources.json. See README.breadboard.ru-RU.md. Source: https://github.com/fritzing/fritzing-parts/blob/develop/core/LED-generic-5mm_6852162_005.fzp; CC BY-SA 3.0
  R4: OpenBot DIY: bundled Fritzing library artwork adapted to the existing connector IDs. Original author and license: library-parts/sources.json. See README.breadboard.ru-RU.md. Source: https://github.com/fritzing/fritzing-parts/blob/develop/core/resistor.fzp; CC BY-SA 3.0
  LED R · правый: OpenBot DIY: bundled Fritzing library artwork adapted to the existing connector IDs. Original author and license: library-parts/sources.json. See README.breadboard.ru-RU.md. Source: https://github.com/fritzing/fritzing-parts/blob/develop/core/LED-generic-5mm_6852162_005.fzp; CC BY-SA 3.0
  OpenBot DIY · Arduino Nano: OpenBot DIY: bundled Fritzing library artwork adapted to the existing connector IDs. Original author and license: library-parts/sources.json. See README.breadboard.ru-RU.md.
  Примечания: OpenBot DIY: bundled Fritzing library artwork adapted to the existing connector IDs. Original author and license: library-parts/sources.json. See README.breadboard.ru-RU.md.
  Цвета проводов: OpenBot DIY: bundled Fritzing library artwork adapted to the existing connector IDs. Original author and license: library-parts/sources.json. See README.breadboard.ru-RU.md.
  Распределитель 6 × 2: OpenBot DIY: bundled Fritzing library artwork adapted to the existing connector IDs. Original author and license: library-parts/sources.json. See README.breadboard.ru-RU.md.
  Соединение VBAT: Native electrical branch contact; CC BY-SA 3.0.
  Соединение ADC: Native electrical branch contact; CC BY-SA 3.0.
