# Fritzing sketch openbot-diy-power-hub (saved by Fritzing 1.0.8)

parts:
  Battery_·_3S = Battery · 3S [part_number="3 × 18650 · 3S"]
  SW1_·_Power = SW1 · Power [part_number="SW1 · питание"]
  L298N_·_Power = L298N · Power [part_number="L298N · три линии питания"]
  POWER_BOARD = POWER BOARD [part_number="POWER BOARD"]
  DISTRIBUTION_·_6_×_2 = DISTRIBUTION · 6 × 2 [part_number="DISTRIBUTION · 6 × 2"]
  R1_·_20_kΩ = R1 · 20 kΩ [part_number=R1]
  R2_·_10_kΩ = R2 · 10 kΩ [part_number=R2]
  OpenBot_DIY_·_Power_hub = OpenBot DIY · Power hub [part_number=heading]  # not connected
  J4_→_Nano = J4 → Nano [part_number=nano_note]  # not connected
  Notes = Notes [part_number=footer]  # not connected

nets:
  N1: Battery_·_3S.+, SW1_·_Power.IN, SW1_·_Power.OUT, L298N_·_Power.+12V, POWER_BOARD.BAT+, POWER_BOARD.SW_IN, POWER_BOARD.SW_OUT, POWER_BOARD.VBAT_L298N, POWER_BOARD.VBAT_R1, R1_·_20_kΩ.1
  GND: Battery_·_3S.GND, L298N_·_Power.GND, POWER_BOARD.GND_BAT, POWER_BOARD.GND_L298N, POWER_BOARD.GND_NANO, POWER_BOARD.GND_periferial, POWER_BOARD.GND_R2, DISTRIBUTION_·_6_×_2.GND_IN, DISTRIBUTION_·_6_×_2.GND_OLED, DISTRIBUTION_·_6_×_2.GND_HC-SR04, DISTRIBUTION_·_6_×_2.GND_FC-03_L, DISTRIBUTION_·_6_×_2.GND_FC-03_R, DISTRIBUTION_·_6_×_2.GND_spare, R2_·_10_kΩ.2
  N2: L298N_·_Power.5V, POWER_BOARD.5V_L298N, POWER_BOARD.5V_periferial, DISTRIBUTION_·_6_×_2.5V_IN, DISTRIBUTION_·_6_×_2.5V_OLED, DISTRIBUTION_·_6_×_2.5V_HC-SR04, DISTRIBUTION_·_6_×_2.5V_FC-03_L, DISTRIBUTION_·_6_×_2.5V_FC-03_R, DISTRIBUTION_·_6_×_2.5V_spare
  N3: POWER_BOARD.A7_NANO, R1_·_20_kΩ.2, R2_·_10_kΩ.1

custom parts:
  Battery · 3S: OpenBot DIY: bundled Fritzing library artwork adapted to the existing connector IDs. Original author and license: library-parts/sources.json. See README.breadboard.ru-RU.md. Source: https://forum.fritzing.org/t/18650-battery-holder-part-design/6523/32; Published Fritzing part; no explicit license in FZP
  SW1 · Power: OpenBot DIY: bundled Fritzing library artwork adapted to the existing connector IDs. Original author and license: library-parts/sources.json. See README.breadboard.ru-RU.md. Source: https://github.com/fritzing/fritzing-parts/blob/develop/core/basic-toggle-switch.fzp; CC BY-SA 3.0
  L298N · Power: OpenBot detachable power module wiring. CC BY-SA 3.0. Artwork credits: Fritzing core, Peter Van Epp. Wiring and layout only; no manufacturing PCB view.
  POWER BOARD: OpenBot detachable power module wiring. CC BY-SA 3.0. Artwork credits: Fritzing core, Peter Van Epp. Wiring and layout only; no manufacturing PCB view.
  DISTRIBUTION · 6 × 2: OpenBot detachable power module wiring. CC BY-SA 3.0. Artwork credits: Fritzing core, Peter Van Epp. Wiring and layout only; no manufacturing PCB view.
  R1 · 20 kΩ: OpenBot DIY: bundled Fritzing library artwork adapted to the existing connector IDs. Original author and license: library-parts/sources.json. See README.breadboard.ru-RU.md. Source: https://github.com/fritzing/fritzing-parts/blob/develop/core/resistor.fzp; CC BY-SA 3.0
  R2 · 10 kΩ: OpenBot DIY: bundled Fritzing library artwork adapted to the existing connector IDs. Original author and license: library-parts/sources.json. See README.breadboard.ru-RU.md. Source: https://github.com/fritzing/fritzing-parts/blob/develop/core/resistor.fzp; CC BY-SA 3.0
  OpenBot DIY · Power hub: OpenBot detachable power module wiring. CC BY-SA 3.0. Artwork credits: Fritzing core, Peter Van Epp. Wiring and layout only; no manufacturing PCB view.
  J4 → Nano: OpenBot detachable power module wiring. CC BY-SA 3.0. Artwork credits: Fritzing core, Peter Van Epp. Wiring and layout only; no manufacturing PCB view.
  Notes: OpenBot detachable power module wiring. CC BY-SA 3.0. Artwork credits: Fritzing core, Peter Van Epp. Wiring and layout only; no manufacturing PCB view.
